// Logisim project ProgramCounter.circ as structural Verilog: 1 circuit, main circuit ProgramCounter
module ProgramCounter (
  input  [31:0] PC_in,
  input  En,
  input  CLK,
  output [31:0] PC_out
);

  Register #(.width(32)) PC (.D(PC_in), .en(En), .clk(CLK), .Q(PC_out));  // open: clr
endmodule
