// Logisim project block.circ as structural Verilog: 1 circuit, main circuit B_lock
module B_lock (
  input  [31:0] data_in,
  input  [1:0] word_index,
  input  CLOCK,
  input  RESET
);

  wire and_1_out, and_2_out, and_3_out, and_4_out, decoder_1_out0, decoder_1_out1, decoder_1_out2,
       decoder_1_out3;

  Decoder #(.select(2)) decoder_1 (
    .out0(decoder_1_out0), .out1(decoder_1_out1), .out2(decoder_1_out2), .out3(decoder_1_out3),
    .sel(word_index), .en(1'b1));
  and and_1 (and_1_out, CLOCK, decoder_1_out0);
  and and_2 (and_2_out, CLOCK, decoder_1_out1);
  and and_3 (and_3_out, CLOCK, decoder_1_out2);
  and and_4 (and_4_out, CLOCK, decoder_1_out3);
  Register register_1 (.D(data_in[7:0]), .en(1'b1), .clk(and_1_out), .clr(RESET));  // open: Q
  Register register_2 (.D(data_in[7:0]), .en(1'b1), .clk(and_2_out), .clr(RESET));  // open: Q
  Register register_3 (.D(data_in[7:0]), .en(1'b1), .clk(and_3_out), .clr(RESET));  // open: Q
  Register register_4 (.D(data_in[7:0]), .en(1'b1), .clk(and_4_out), .clr(RESET));  // open: Q
  Register register_5 (.D(data_in[15:8]), .en(1'b1), .clk(and_1_out), .clr(RESET));  // open: Q
  Register register_6 (.D(data_in[15:8]), .en(1'b1), .clk(and_2_out), .clr(RESET));  // open: Q
  Register register_7 (.D(data_in[15:8]), .en(1'b1), .clk(and_3_out), .clr(RESET));  // open: Q
  Register register_8 (.D(data_in[15:8]), .en(1'b1), .clk(and_4_out), .clr(RESET));  // open: Q
  Register register_9 (.D(data_in[23:16]), .en(1'b1), .clk(and_1_out), .clr(RESET));  // open: Q
  Register register_10 (.D(data_in[23:16]), .en(1'b1), .clk(and_2_out), .clr(RESET));  // open: Q
  Register register_11 (.D(data_in[23:16]), .en(1'b1), .clk(and_3_out), .clr(RESET));  // open: Q
  Register register_12 (.D(data_in[23:16]), .en(1'b1), .clk(and_4_out), .clr(RESET));  // open: Q
  Register register_13 (.D(data_in[31:24]), .en(1'b1), .clk(and_1_out), .clr(RESET));  // open: Q
  Register register_14 (.D(data_in[31:24]), .en(1'b1), .clk(and_2_out), .clr(RESET));  // open: Q
  Register register_15 (.D(data_in[31:24]), .en(1'b1), .clk(and_3_out), .clr(RESET));  // open: Q
  Register register_16 (.D(data_in[31:24]), .en(1'b1), .clk(and_4_out), .clr(RESET));  // open: Q

  // Notes on the sheet:
  //   w3
  //   w1
  //   w2
  //   w4
endmodule
