// Logisim project cache.circ as structural Verilog: 1 circuit, main circuit cache
module cache (
  input  [13:0] CPU_Address,
  input  block_index,
  input  [31:0] data_in,
  input  [3:0] MemWriteMask,
  input  Hit,
  input  LRU,
  input  clock,
  input  reset,
  input  LRU_out,
  output [31:0] raedData
);

  wire and_5_out, and_6_out, and_7_out, and_8_out, and_9_out, and_10_out, and_11_out, and_12_out, and_13_out,
       and_14_out, and_15_out, and_16_out, and_17_out, and_18_out, and_19_out, and_20_out, and_21_out,
       and_22_out, clock1, clock2, clock3, clock4, comparator_1_eq, comparator_2_eq, comparator_3_eq,
       comparator_4_eq, comparator_5_eq, comparator_6_eq, comparator_7_eq, comparator_8_eq, dirty_b11,
       dirty_b12, dirty_b21, dirty_b22, dirty_b31, dirty_b32, dirty_b41, dirty_b42, hit1, hit2, hit3, hit4,
       not_1_out, not_2_out, not_3_out, not_4_out, not_5_out, not_6_out, not_7_out, not_8_out, not_9_out,
       not_10_out, set1, set2, set3, set4, v11, v12, v21, v22, v31, v32, v41, v42;
  wire [9:0] register_17_q, register_18_q, register_19_q, register_20_q, register_21_q, register_22_q,
       register_23_q, register_24_q;

  Decoder #(.select(2)) decoder_1 (
    .out0(set1), .out1(set2), .out2(set3), .out3(set4), .sel(CPU_Address[11:10]), .en(1'b1));
  and and_1 (clock1, clock, set1);
  and and_2 (clock2, clock, set2);
  and and_3 (clock3, clock, set3);
  set set_1 (
    .data_in(data_in), .word_index(CPU_Address[13:12]), .block_index(block_index),
    .MemWriteMask(MemWriteMask), .CLOCK(clock1), .RESET(reset), .MemReadData(raedData));
  set set_2 (
    .data_in(data_in), .word_index(CPU_Address[13:12]), .block_index(block_index),
    .MemWriteMask(MemWriteMask), .CLOCK(clock2), .RESET(reset), .MemReadData(raedData));
  set set_3 (
    .data_in(data_in), .word_index(CPU_Address[13:12]), .block_index(block_index),
    .MemWriteMask(MemWriteMask), .CLOCK(clock3), .RESET(reset), .MemReadData(raedData));
  set set_4 (
    .data_in(data_in), .word_index(CPU_Address[13:12]), .block_index(block_index),
    .MemWriteMask(MemWriteMask), .CLOCK(clock4), .RESET(reset), .MemReadData(raedData));
  and and_4 (clock4, clock, set4);
  or or_1 (Hit, hit1, hit2, hit3, hit4);
  not not_1 (not_1_out, Hit);
  not not_2 (not_2_out, LRU);
  and and_5 (and_5_out, not_1_out, not_2_out);
  and and_6 (and_6_out, LRU, Hit);
  Register #(.width(1)) register_1 (.en(1'b1), .clk(clock1), .Q(v11), .clr(reset));  // open: D
  Register #(.width(1)) register_2 (.en(1'b1), .clk(clock1), .Q(v12), .clr(reset));  // open: D
  Register #(.width(1)) register_3 (.en(1'b1), .clk(clock2), .Q(v21), .clr(reset));  // open: D
  Register #(.width(1)) register_4 (.en(1'b1), .clk(clock2), .Q(v22), .clr(reset));  // open: D
  Register #(.width(1)) register_5 (.en(1'b1), .clk(clock3), .Q(v31), .clr(reset));  // open: D
  Register #(.width(1)) register_6 (.en(1'b1), .clk(clock3), .Q(v32), .clr(reset));  // open: D
  Register #(.width(1)) register_7 (.en(1'b1), .clk(clock4), .Q(v41), .clr(reset));  // open: D
  Register #(.width(1)) register_8 (.en(1'b1), .clk(clock4), .Q(v42), .clr(reset));  // open: D
  or or_2 (LRU_out, and_6_out, and_5_out);
  Register #(.width(1)) register_9 (.en(1'b1), .clk(clock1), .Q(dirty_b11), .clr(reset));  // open: D
  Register #(.width(1)) register_10 (.en(1'b1), .clk(clock1), .Q(dirty_b12), .clr(reset));  // open: D
  Register #(.width(1)) register_11 (.en(1'b1), .clk(clock2), .Q(dirty_b21), .clr(reset));  // open: D
  Register #(.width(1)) register_12 (.en(1'b1), .clk(clock2), .Q(dirty_b22), .clr(reset));  // open: D
  Register #(.width(1)) register_13 (.en(1'b1), .clk(clock3), .Q(dirty_b31), .clr(reset));  // open: D
  Register #(.width(1)) register_14 (.en(1'b1), .clk(clock3), .Q(dirty_b32), .clr(reset));  // open: D
  Register #(.width(1)) register_15 (.en(1'b1), .clk(clock4), .Q(dirty_b41), .clr(reset));  // open: D
  Register #(.width(1)) register_16 (.en(1'b1), .clk(clock4), .Q(dirty_b42), .clr(reset));  // open: D
  not not_3 (not_3_out, LRU);
  not not_4 (not_4_out, LRU);
  not not_5 (not_5_out, LRU);
  not not_6 (not_6_out, LRU);
  and and_7 (and_7_out, not_7_out, not_3_out);
  and and_8 (and_8_out, not_7_out, LRU);
  and and_9 (and_9_out, not_8_out, not_4_out);
  and and_10 (and_10_out, not_8_out, LRU);
  and and_11 (and_11_out, not_9_out, not_5_out);
  and and_12 (and_12_out, not_9_out, LRU);
  and and_13 (and_13_out, not_10_out, not_6_out);
  and and_14 (and_14_out, not_10_out, LRU);
  Register #(.width(10)) register_17 (
    .D(CPU_Address[9:0]), .en(and_7_out), .clk(clock1), .Q(register_17_q), .clr(reset));
  Register #(.width(10)) register_18 (
    .D(CPU_Address[9:0]), .en(and_8_out), .clk(clock1), .Q(register_18_q), .clr(reset));
  Register #(.width(10)) register_19 (
    .D(CPU_Address[9:0]), .en(and_9_out), .clk(clock2), .Q(register_19_q), .clr(reset));
  Register #(.width(10)) register_20 (
    .D(CPU_Address[9:0]), .en(and_10_out), .clk(clock2), .Q(register_20_q), .clr(reset));
  Register #(.width(10)) register_21 (
    .D(CPU_Address[9:0]), .en(and_11_out), .clk(clock3), .Q(register_21_q), .clr(reset));
  Register #(.width(10)) register_22 (
    .D(CPU_Address[9:0]), .en(and_12_out), .clk(clock3), .Q(register_22_q), .clr(reset));
  Register #(.width(10)) register_23 (
    .D(CPU_Address[9:0]), .en(and_13_out), .clk(clock4), .Q(register_23_q), .clr(reset));
  Register #(.width(10)) register_24 (
    .D(CPU_Address[9:0]), .en(and_14_out), .clk(clock4), .Q(register_24_q), .clr(reset));
  Comparator #(.mode("unsigned"), .width(10)) comparator_1 (
    .a(register_17_q), .b(CPU_Address[9:0]), .eq(comparator_1_eq));  // open: gt, lt
  Comparator #(.mode("unsigned"), .width(10)) comparator_2 (
    .a(register_18_q), .b(CPU_Address[9:0]), .eq(comparator_2_eq));  // open: gt, lt
  Comparator #(.mode("unsigned"), .width(10)) comparator_3 (
    .a(register_19_q), .b(CPU_Address[9:0]), .eq(comparator_3_eq));  // open: gt, lt
  Comparator #(.mode("unsigned"), .width(10)) comparator_4 (
    .a(register_20_q), .b(CPU_Address[9:0]), .eq(comparator_4_eq));  // open: gt, lt
  Comparator #(.mode("unsigned"), .width(10)) comparator_5 (
    .a(register_21_q), .b(CPU_Address[9:0]), .eq(comparator_5_eq));  // open: gt, lt
  Comparator #(.mode("unsigned"), .width(10)) comparator_6 (
    .a(register_22_q), .b(CPU_Address[9:0]), .eq(comparator_6_eq));  // open: gt, lt
  Comparator #(.mode("unsigned"), .width(10)) comparator_7 (
    .a(register_23_q), .b(CPU_Address[9:0]), .eq(comparator_7_eq));  // open: gt, lt
  Comparator #(.mode("unsigned"), .width(10)) comparator_8 (
    .a(register_24_q), .b(CPU_Address[9:0]), .eq(comparator_8_eq));  // open: gt, lt
  not not_7 (not_7_out, hit1);
  and and_15 (and_15_out, v11, comparator_1_eq);
  and and_16 (and_16_out, v12, comparator_2_eq);
  not not_8 (not_8_out, hit2);
  and and_17 (and_17_out, v21, comparator_3_eq);
  and and_18 (and_18_out, v22, comparator_4_eq);
  not not_9 (not_9_out, hit3);
  and and_19 (and_19_out, v31, comparator_5_eq);
  and and_20 (and_20_out, v32, comparator_6_eq);
  not not_10 (not_10_out, hit4);
  and and_21 (and_21_out, v41, comparator_7_eq);
  and and_22 (and_22_out, v42, comparator_8_eq);
  or or_3 (hit1, and_15_out, and_16_out);
  or or_4 (hit2, and_17_out, and_18_out);
  or or_5 (hit3, and_19_out, and_20_out);
  or or_6 (hit4, and_21_out, and_22_out);

  // Other names for the same wires on the sheet: tag[9:0] = CPU_Address[9:0]; set_index[1:0] = CPU_Address[11:10];
  //   word_index[1:0] = CPU_Address[13:12]; readData[31:0] = raedData

  // Notes on the sheet:
  //   tag: 10 bit, set: 2bit, word: 2bit
  //   valid bit
  //   valid bit
  //   valid bit
  //   valid bit
  //   dirty bit
  //   dirty bit
  //   dirty bit
  //   dirty bit
  //   set1
  //   set2
  //   set3
  //   set4
  //   tag array
  //   tag array
  //   tag array
  //   tag array
endmodule
