// Logisim project cpu.circ as structural Verilog: 1 circuit, main circuit cpu
module cpu (
  input  reset,
  input  in_2
);

  wire alu_1_zero, alu_2_zero, ALU_v, ALUSrc, ALUSrc_out, ALUv_out, and_1_out, and_2_out, Branch, BranchOut,
       cache_1_hit, cache_1_lru_out, cahcecu_1_lru_out, cahcecu_2_lru_out, clk, clk_main, clk_out, Hit, JAL,
       Jump, Jump_out, LRU_OUT, MemToReg, MemToReg_out, multiplexer_11_out, not_1_out, not_2_out, not_3_out,
       not_4_out, RegDst, RegDst_out, RegWrite, RegWrite_out, syscall, syscall_out;
  wire [3:0] cache_1_writemask, MemWriteMask, MemWriteMask_out, writeMask_cache;
  wire [4:0] instSplitter_rd, instSplitter_rs, instSplitter_rt, instSplitter_shamt, multiplexer_3_out,
       multiplexer_4_out, multiplexer_7_out, multiplexer_8_out, rd, rd_out, rs, rs_out, rt, rt_out, shamt,
       shamt_out;
  wire [5:0] ALU_op, ALUop_out, func, funcOut, instSplitter_func, instSplitter_op, opcode, opcode_out;
  wire [15:0] imm16, immOut, instSplitter_imm16;
  wire [25:0] instSplitter_target26, target26, target26_out;
  wire [27:0] sxl2_1_t28, SXL_2_t28;
  wire [31:0] adder_1_out, adder_3_out, adder_4_out, alu_1_aluresult, ALUResult, ALUResult_out, BResult,
       BResult_out, cache_1_raeddata, cacheOut, DataMem_memreaddata, immIN, immINout, in1, in1_out, in2,
       in2_out, instMem_memreaddata, jcu_1_y, JCU_OUT, Jcu_outF, memdelayed_1_memreaddata, multiplexer_1_out,
       multiplexer_5_out, multiplexer_6_out, multiplexer_9_out, multiplexer_10_out, multiplexer_12_out,
       multiplexer_14_out, outMM, PC_pc_out, programcounter_1_pc_out, RD1, RD1_out, RD2, RD2_out,
       RegisterFile_readdata1, RegisterFile_readdata2, SE_s32, shifter_1_out, shifter_2_out, writeback,
       writeback_out;

  not not_1 (not_1_out, syscall);
  not not_2 (not_2_out, syscall_out);
  ProgramCounter PC (.PC_in(jcu_1_y), .En(not_1_out), .CLK(multiplexer_11_out), .PC_out(PC_pc_out));
  Adder #(.width(32)) adder_1 (.a(PC_pc_out), .b(32'h4), .out(adder_1_out));  // open: cin, cout
  ProgramCounter programcounter_1 (.PC_in(JCU_OUT), .En(not_2_out), .CLK(clk), .PC_out(programcounter_1_pc_out));
  Adder #(.width(32)) adder_2 (.a(programcounter_1_pc_out), .b(32'h4), .out(in2));  // open: cin, cout
  Multiplexer #(.width(32)) multiplexer_1 (
    .in0(multiplexer_6_out), .in1({adder_1_out[31:28], SXL_2_t28}), .out(multiplexer_1_out), .sel(Jump));
  memDelayed instMem (
    .MemAddress(PC_pc_out), .clk(multiplexer_11_out), .MemReadData(instMem_memreaddata));  // open: MemWriteMask, MemWriteData
  Multiplexer #(.width(32)) multiplexer_2 (
    .in0(BResult_out), .in1({in2[31:28], sxl2_1_t28}), .out(in1), .sel(Jump_out));
  SXL2 SXL_2 (.T26(instSplitter_target26), .T28(SXL_2_t28));
  SXL2 sxl2_1 (.T26(target26), .T28(sxl2_1_t28));
  memDelayed memdelayed_1 (
    .MemAddress(programcounter_1_pc_out), .clk(clk), .MemReadData(memdelayed_1_memreaddata));  // open: MemWriteMask, MemWriteData
  instruction_splitter instSplitter (
    .instruction(instMem_memreaddata), .op(instSplitter_op), .target26(instSplitter_target26),
    .rs(instSplitter_rs), .rt(instSplitter_rt), .imm16(instSplitter_imm16), .rd(instSplitter_rd),
    .shamt(instSplitter_shamt), .func(instSplitter_func));
  instruction_splitter instruction_splitter_1 (
    .instruction(memdelayed_1_memreaddata), .op(opcode), .target26(target26), .rs(rs), .rt(rt),
    .imm16(imm16), .rd(rd), .shamt(shamt), .func(func));
  Multiplexer #(.width(5)) multiplexer_3 (
    .in0(instSplitter_rt), .in1(instSplitter_rd), .out(multiplexer_3_out), .sel(RegDst));
  Multiplexer #(.width(5)) multiplexer_4 (.in0(multiplexer_3_out), .in1({5{1'b1}}), .out(multiplexer_4_out), .sel(JAL));
  JCU jcu_1 (.Func(instSplitter_func), .in1(multiplexer_1_out), .rs(instSplitter_rs), .Y(jcu_1_y));
  Multiplexer #(.width(32)) multiplexer_5 (.in0(multiplexer_12_out), .in1(jcu_1_y), .out(multiplexer_5_out), .sel(JAL));
  CU ControlUnit (
    .Func(instSplitter_func), .Opcode(instSplitter_op), .JAL(JAL), .ALUSrc(ALUSrc), .ALUop(ALU_op),
    .syscall(syscall), .RegDst(RegDst), .ALU_V(ALU_v), .MemToReg(MemToReg), .RegWrite(RegWrite),
    .MemWriteMask(MemWriteMask), .Branch(Branch), .Jump(Jump));
  Register #(.width(32)) register_1 (.D(in2), .en(1'b1), .clk(clk), .Q(in2_out));  // open: clr
  Register #(.width(32)) register_2 (.D(in1), .en(1'b1), .clk(clk), .Q(in1_out));  // open: clr
  Register #(.width(6)) register_3 (.D(opcode), .en(1'b1), .clk(clk), .Q(opcode_out));  // open: clr
  Register #(.width(26)) register_4 (.D(target26), .clk(clk), .Q(target26_out));  // open: en, clr
  Register #(.width(5)) register_5 (.D(rs), .en(1'b1), .clk(clk), .Q(rs_out));  // open: clr
  Register #(.width(5)) register_6 (.D(rt), .en(1'b1), .clk(clk), .Q(rt_out));  // open: clr
  Register #(.width(16)) register_7 (.D(imm16), .en(1'b1), .clk(clk), .Q(immOut));  // open: clr
  Register #(.width(5)) register_8 (.D(rd), .en(1'b1), .Q(rd_out));  // open: clk, clr
  Register #(.width(5)) register_9 (.D(shamt), .en(1'b1), .clk(clk), .Q(shamt_out));  // open: clr
  Register #(.width(6)) register_10 (.D(func), .en(1'b1), .clk(clk), .Q(funcOut));  // open: clr
  SignExtend SE (.S16(instSplitter_imm16), .S32(SE_s32));
  regfile RegisterFile (
    .ReadIndex1(instSplitter_rs), .ReadIndex2(instSplitter_rt), .WriteIndex(multiplexer_4_out),
    .WriteData(multiplexer_5_out), .RegWEn(RegWrite), .clk(multiplexer_11_out),
    .ReadData1(RegisterFile_readdata1), .ReadData2(RegisterFile_readdata2));
  Multiplexer #(.width(32)) multiplexer_6 (
    .in0(adder_1_out), .in1(adder_3_out), .out(multiplexer_6_out), .sel(and_1_out));
  Shifter #(.width(32)) shifter_1 (.in(SE_s32), .\dist (5'b00010), .out(shifter_1_out));
  Adder #(.width(32)) adder_3 (.a(adder_1_out), .b(shifter_1_out), .out(adder_3_out));  // open: cin, cout
  Multiplexer #(.width(5)) multiplexer_7 (.in0(rt_out), .in1(rd_out), .out(multiplexer_7_out), .sel(RegDst));
  Multiplexer #(.width(5)) multiplexer_8 (.in0(multiplexer_7_out), .in1({5{1'b1}}), .out(multiplexer_8_out), .sel(JAL));
  JCU jcu_2 (.Func(funcOut), .in1(in1_out), .rs(rs_out), .Y(JCU_OUT));
  Multiplexer #(.width(32)) multiplexer_9 (.in0(writeback_out), .in1(JCU_OUT), .out(multiplexer_9_out), .sel(JAL));
  and and_1 (and_1_out, Branch, alu_1_zero);
  ALU alu_1 (
    .A(RegisterFile_readdata1), .B(RegisterFile_readdata2), .ALUOp(ALU_op), .Func(instSplitter_func),
    .Imm(SE_s32), .Shamt(instSplitter_shamt), .ALUSrc(ALUSrc), .Zero(alu_1_zero), .ALUResult(alu_1_aluresult));
  CU cu_1 (
    .Func(funcOut), .Opcode(opcode_out), .JAL(JAL), .ALUSrc(ALUSrc), .ALUop(ALU_op), .syscall(syscall),
    .RegDst(RegDst), .ALU_V(ALU_v), .MemToReg(MemToReg), .RegWrite(RegWrite), .MemWriteMask(MemWriteMask),
    .Branch(Branch), .Jump(Jump));
  SignExtend signextend_1 (.S16(immOut), .S32(immIN));
  regfile regfile_1 (
    .ReadIndex1(rs_out), .ReadIndex2(rt_out), .WriteIndex(multiplexer_8_out), .WriteData(multiplexer_9_out),
    .RegWEn(RegWrite), .clk(clk), .ReadData1(RD1), .ReadData2(RD2));
  cahceCU cahcecu_1 (
    .CPU_Address(alu_1_aluresult), .LRU(cache_1_lru_out), .CLOCK(multiplexer_11_out), .RESET(reset),
    .LRU_out(cahcecu_1_lru_out));
  Clock u_clk (.out(clk_out));
  Multiplexer #(.width(32)) multiplexer_10 (
    .in0(DataMem_memreaddata), .in1(RegisterFile_readdata2), .out(multiplexer_10_out), .sel(cache_1_hit));
  not not_3 (not_3_out, multiplexer_11_out);
  Register #(.width(32)) register_11 (.D(immIN), .en(1'b1), .clk(clk), .Q(immINout));  // open: clr
  Register #(.width(32)) register_12 (.D(JCU_OUT), .en(1'b1), .clk(clk), .Q(Jcu_outF));  // open: clr
  Register #(.width(1)) register_13 (.D(ALUSrc), .en(1'b1), .clk(clk), .Q(ALUSrc_out));  // open: clr
  Register #(.width(6)) register_14 (.D(ALU_op), .en(1'b1), .clk(clk), .Q(ALUop_out));  // open: clr
  Register #(.width(1)) register_15 (.D(RegDst), .en(1'b1), .clk(clk), .Q(RegDst_out));  // open: clr
  Register #(.width(1)) register_16 (.D(ALU_v), .en(1'b1), .clk(clk), .Q(ALUv_out));  // open: clr
  Register #(.width(1)) register_17 (.D(MemToReg), .en(1'b1), .clk(clk), .Q(MemToReg_out));  // open: clr
  Register #(.width(1)) register_18 (.D(RegWrite), .en(1'b1), .clk(clk), .Q(RegWrite_out));  // open: clr
  Register #(.width(4)) register_19 (.D(MemWriteMask), .en(1'b1), .clk(clk), .Q(MemWriteMask_out));  // open: clr
  Register #(.width(1)) register_20 (.D(Branch), .en(1'b1), .clk(clk), .Q(BranchOut));  // open: clr
  Register #(.width(1)) register_21 (.D(Jump), .en(1'b1), .clk(clk), .Q(Jump_out));  // open: clr
  Register #(.width(32)) register_22 (.D(RD1), .en(1'b1), .clk(clk), .Q(RD1_out));  // open: clr
  Register #(.width(32)) register_23 (.D(RD2), .en(1'b1), .clk(clk), .Q(RD2_out));  // open: clr
  Register #(.width(1)) register_24 (.D(syscall), .en(1'b1), .clk(clk), .Q(syscall_out));  // open: clr
  memDelayed DataMem (
    .MemAddress(alu_1_aluresult), .MemWriteMask(cache_1_writemask), .MemWriteData(RegisterFile_readdata2),
    .clk(not_3_out), .MemReadData(DataMem_memreaddata));
  cache cache_1 (
    .CPU_Address(alu_1_aluresult), .memWriteData(multiplexer_10_out), .MemWriteMask(MemWriteMask),
    .LRU(cahcecu_1_lru_out), .clock(clk_out), .reset(reset), .raedData(cache_1_raeddata), .Hit(cache_1_hit),
    .LRU_out(cache_1_lru_out), .writeMask(cache_1_writemask));
  Multiplexer multiplexer_11 (.in0(1'b0), .in1(clk_out), .out(multiplexer_11_out), .sel(cache_1_hit));
  Multiplexer #(.width(32)) multiplexer_12 (
    .in0(alu_1_aluresult), .in1(cache_1_raeddata), .out(multiplexer_12_out), .sel(MemToReg));
  Multiplexer #(.width(32)) multiplexer_13 (.in0(in2_out), .in1(adder_4_out), .out(BResult), .sel(and_2_out));
  Shifter #(.width(32)) shifter_2 (.in(immINout), .\dist (5'b00010), .out(shifter_2_out));
  Adder #(.width(32)) adder_4 (.a(in2_out), .b(shifter_2_out), .out(adder_4_out));  // open: cin, cout
  ALU alu_2 (
    .A(RD1_out), .B(RD2_out), .ALUOp(ALUop_out), .Func(funcOut), .Imm(immINout), .Shamt(shamt_out),
    .ALUSrc(ALUSrc_out), .Zero(alu_2_zero), .ALUResult(ALUResult));
  and and_2 (and_2_out, BranchOut, alu_2_zero);
  Register #(.width(32)) register_25 (.D(BResult), .en(1'b1), .clk(clk), .Q(BResult_out));  // open: clr
  Register #(.width(32)) register_26 (.D(ALUResult), .en(1'b1), .clk(clk), .Q(ALUResult_out));  // open: clr
  not not_4 (not_4_out, clk);
  cahceCU cahcecu_2 (
    .CPU_Address(ALUResult_out), .LRU(LRU_OUT), .CLOCK(clk), .RESET(in_2), .LRU_out(cahcecu_2_lru_out));
  Multiplexer #(.width(32)) multiplexer_14 (.in0(outMM), .in1(RD2_out), .out(multiplexer_14_out), .sel(Hit));
  Clock clock_1 (.out(clk_main));
  memDelayed memdelayed_2 (
    .MemAddress(ALUResult_out), .MemWriteMask(writeMask_cache), .MemWriteData(RD2_out), .clk(not_4_out),
    .MemReadData(outMM));
  cache cache_2 (
    .CPU_Address(ALUResult_out), .memWriteData(multiplexer_14_out), .MemWriteMask(MemWriteMask_out),
    .LRU(cahcecu_2_lru_out), .clock(clk_main), .reset(in_2), .raedData(cacheOut), .Hit(Hit),
    .LRU_out(LRU_OUT), .writeMask(writeMask_cache));
  Multiplexer multiplexer_15 (.in0(1'b0), .in1(clk_main), .out(clk), .sel(Hit));
  Multiplexer #(.width(32)) multiplexer_16 (.in0(ALUResult_out), .in1(cacheOut), .out(writeback), .sel(MemToReg_out));
  Register #(.width(32)) register_27 (.D(writeback), .en(1'b1), .clk(clk), .Q(writeback_out));  // open: clr

  // Other names for the same wires on the sheet: reset_t = in_2
endmodule
